# Fritzing sketch doan (saved by Fritzing 0.9.3b)
breadboards: 5

parts:
  R1 = Resistor [tolerance=±5% resistance=56k package=THT]
  U1 = 555 Timer [package="SO8 [SMD]"]  # not connected
  C1 = Electrolytic Capacitor [capacitance=1µF package="100 mil [THT, electrolytic]"]
  IC2 = IC, DIP package, 16 pins [chip_label=IC7447]
  R3 = Resistor [tolerance=±5% resistance=220 package=THT]
  R4 = Resistor [tolerance=±5% resistance=220 package=THT]
  R5 = Resistor [tolerance=±5% resistance=220 package=THT]
  R6 = Resistor [tolerance=±5% resistance=220 package=THT]
  R7 = Resistor [tolerance=±5% resistance=220 package=THT]
  R8 = Resistor [tolerance=±5% resistance=220 package=THT]
  R9 = Resistor [tolerance=±5% resistance=220 package=THT]
  DI1 = 7-Segment LED Display [package=THT]
  IC3 = IC, DIP package, 16 pins [chip_label=IC74192]
  IC4 = IC, DIP package, 16 pins [chip_label=IC7447]
  R10 = Resistor [tolerance=±5% resistance=220 package=THT]
  R11 = Resistor [tolerance=±5% resistance=220 package=THT]
  R12 = Resistor [tolerance=±5% resistance=220 package=THT]
  R13 = Resistor [tolerance=±5% resistance=220 package=THT]
  R14 = Resistor [tolerance=±5% resistance=220 package=THT]
  R15 = Resistor [tolerance=±5% resistance=220 package=THT]
  R16 = Resistor [tolerance=±5% resistance=220 package=THT]
  DI2 = 7-Segment LED Display [package=THT]
  R17 = Trimmer Potentiometer [maximum_resistance=10kΩ package=THT]
  IC1 = IC, DIP package, 16 pins [chip_label=IC74192]

nets:
  N1: R1.Pin_1, C1.-, R17.leg1, R17.wiper, R17.leg2
  N2: IC2.pin1, IC1.pin2
  N3: IC2.pin2, IC1.pin6
  N4: IC2.pin3, IC2.pin4, IC2.pin5, IC2.pin8, IC1.pin1, IC1.pin8
  N5: IC2.pin6, IC1.pin7
  N6: IC2.pin7, IC1.pin3
  N7: IC2.pin9, R7.Pin_1
  N8: IC2.pin10, R8.Pin_1
  N9: IC2.pin11, R9.Pin_1
  N10: IC2.pin12, R6.Pin_0
  N11: IC2.pin13, R5.Pin_0
  N12: IC2.pin14, R3.Pin_0
  N13: IC2.pin15, R4.Pin_0
  N14: IC2.pin16, DI1.commAnode#7, IC1.pin11, IC1.pin16
  N15: R3.Pin_1, DI1.cathodeG
  N16: R4.Pin_1, DI1.cathodeF
  N17: R6.Pin_1, DI1.cathodeB
  N18: R7.Pin_0, DI1.cathodeE
  N19: R8.Pin_0, DI1.cathodeD
  N20: R9.Pin_0, DI1.cathodeC
  N21: IC3.pin1, IC3.pin8
  N22: IC3.pin2, IC4.pin1
  N23: IC3.pin3, IC4.pin7
  N24: IC3.pin5, IC1.pin12
  N25: IC3.pin6, IC4.pin2
  N26: IC3.pin7, IC4.pin6
  N27: IC3.pin9, IC3.pin10, IC3.pin14, IC3.pin15
  N28: IC3.pin11, IC3.pin16, IC4.pin16, DI2.commAnode#7
  N29: IC4.pin3, IC4.pin4, IC4.pin5, IC4.pin8
  N30: IC4.pin9, R14.Pin_1
  N31: IC4.pin10, R15.Pin_1
  N32: IC4.pin11, R16.Pin_1
  N33: IC4.pin12, R13.Pin_0
  N34: IC4.pin13, R12.Pin_0
  N35: IC4.pin14, R11.Pin_0
  N36: IC4.pin15, R10.Pin_0
  N37: R10.Pin_1, DI2.cathodeF
  N38: R11.Pin_1, DI2.cathodeG
  N39: R12.Pin_1, DI2.cathodeA
  N40: R13.Pin_1, DI2.cathodeB
  N41: R14.Pin_0, DI2.cathodeE
  N42: R15.Pin_0, DI2.cathodeD
  N43: R16.Pin_0, DI2.cathodeC
  N44: IC1.pin9, IC1.pin10, IC1.pin14, IC1.pin15

notes:
  Dây đỏ : nguồn
  Dây đen: mass
